# Fritzing sketch Untitled Sketch 2 (saved by Fritzing 0.9.3b)
breadboards: 1

parts:
  S1 = Pushbutton [package="[THT]"]
  S2 = Pushbutton [package="[THT]"]
  S3 = Pushbutton [package="[THT]"]
  S4 = Pushbutton [package="[THT]"]
  LCD1 = LCD screen
  U1 = TEMPERATURE-SENSOR [package=to-92]
  U2 = POT [package=pot_mammoth]
  LED1 = smd LED [color="Red (633nm)" package="0603 [SMD]"]
  part = Resistor [tolerance=±5% resistance=10k package=THT]
  part_2 = Resistor [tolerance=±5% resistance=10k package=THT]
  part_3 = Resistor [tolerance=±5% resistance=10k package=THT]
  part_4 = Resistor [tolerance=±5% resistance=10k package=THT]
  part_5 = Resistor [tolerance=±5% resistance=220 package=THT]
  R2 = Resistor [tolerance=±5% resistance=4.7k package=THT]
  Part1 = Arduino Leonardo (Rev3b)

nets:
  N1: S1.Pin_1, S1.Pin_2, part.Pin_1
  VDD: S1.Pin_3, S1.Pin_4, S2.Pin_3, S2.Pin_4, S3.Pin_3, S3.Pin_4, S4.Pin_3, S4.Pin_4, LCD1.VDD, LCD1.LED+, U1.VCC, U2.E, R2.Pin_0, Part1.5V
  N2: S2.Pin_1, S2.Pin_2, part_2.Pin_1
  N3: S3.Pin_1, S3.Pin_2, part_3.Pin_1
  N4: S4.Pin_1, S4.Pin_2, part_4.Pin_1
  GND: LCD1.VSS, LCD1.R/W, LCD1.LED-, U1.GND, U2.S, LED1.cathode, part.Pin_0, part_2.Pin_0, part_3.Pin_0, part_4.Pin_0, Part1.GND
  N5: LCD1.V0, U2.A
  N6: LCD1.E, Part1.D11_PWM
  N7: LCD1.DB4, Part1.D7
  N8: LCD1.DB5, Part1.D8/A8
  N9: LCD1.DB6, Part1.D9_PWM/A9
  N10: LCD1.DB7, Part1.D10_PWM/A10
  N11: U1.ADJ, R2.Pin_1, Part1.D4/A6
  N12: LED1.anode, part_5.Pin_0
  N13: part_5.Pin_1, Part1.D6_PWM/A7

notes:
  Pin 0
  Pin 1
  Pin 2
  Pin 3
  Przekaźnik
